# Fritzing sketch Autohelm 800 ESP32 Retrofit (saved by Fritzing 0.9.6b)
circuit board: 8.46667cm x 5.64444cm

parts:
  L298N1 = L298N DC motor driver
  JP1 = Header 5x2 [package=avr_icsp]
  LOLIN32_LITE = Wemos Lolin32lite
  J1 = Power Jack [package=power_jack_smd]
  M1 = DC Motor
  U2 = Mini-360 DC-DC Buck converter [package=THT]
  Mod2 = MAX-471 [package=THT]

nets:
  N1: L298N1.OUT1, M1.pin_2
  N2: L298N1.OUT2, M1.pin_1
  12V: L298N1.12V, LOLIN32_LITE.pin_26, J1.GND, Mod2.vout, Mod2.gnd#2, Mod2.AT
  N3: L298N1.GND, U2.IN-, Mod2.gnd#0
  N4: L298N1.5V, U2.IN+
  N5: L298N1.ENA, LOLIN32_LITE.pin_22
  N6: L298N1.IN1, LOLIN32_LITE.pin_21
  N7: L298N1.IN2, LOLIN32_LITE.pin_20
  N8: JP1.3, LOLIN32_LITE.pin_16
  N9: JP1.5, LOLIN32_LITE.pin_10
  N10: JP1.6, LOLIN32_LITE.pin_9
  N11: JP1.7, LOLIN32_LITE.pin_11
  N12: JP1.8, LOLIN32_LITE.pin_13, Mod2.gnd#6, Mod2.gnd#7
  N13: JP1.9, LOLIN32_LITE.pin_12
  N14: JP1.10, LOLIN32_LITE.pin_8
  N15: LOLIN32_LITE.pin_14, U2.OUT+
  N16: LOLIN32_LITE.pin_15, U2.OUT-
  N17: LOLIN32_LITE.pin_27, Mod2.VT
  N18: J1.GNDBREAK, Mod2.vin

notes:
  Keypad V2

custom parts:
  L298N DC motor driver: 2x DC motor driver with 78M05 positive voltage regulator (7..35 V) L298N: max 46 V, 2 A Set 5 V Enable jumper to enable 5 V regultor (needed for the L298N) and +5 V output at screw terminal or supply external +5 V at screw terminal Set ENA and/or ENB to +5 V to enable motor permanently or supply ENA and/or ENB with PWM signal IN1 and IN2 set rotation directory for motor A (OUT1/OUT2) IN2 and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
  Wemos Lolin32lite: Wemos Lolinlite32 wifi and blue tooth board based on the ESP-32 cpu, digital I/Os 19, analog inputs 6, clock 240mhz, Flash 4Mbytes, lipo battery charger (500ma connection broken out on breadboard but not pcb), usb.
  Mini-360 DC-DC Buck converter: Mini-360 DC-DC Buck converter. Tiny buck step down voltage converter, input voltage 4.75 to 23V output 1 to 17V adjustable. Available from ebay and the like.
  MAX-471: MAX471 Current detection module. 3-36V, 0-3A
